# Fritzing sketch Sender (saved by Fritzing 0.9.3b)
breadboards: 1

parts:
  U1 = attiny85 [package=dip]
  BAT2 = Battery Holders [package=battcom_20mm_pth]
  S1 = Pushbutton [package="[THT]"]
  R1 = Resistor [tolerance=±5% resistance=220 package="0805 [SMD]"]
  R2 = Resistor [tolerance=±5% resistance=10k package="0805 [SMD]"]
  LED1 = LED - 5mm [color="Red (633nm)" package="5 mm [THT]"]
  Mod1 = KY-005 Infrared Transmitter Module [package="Breakout board"]

nets:
  N1: U1.Pin_3, Mod1.S
  N2: U1.Pin_4, BAT2.-, R1.Pin_0, R2.Pin_0, Mod1.-
  N3: U1.Pin_5, S1.Pin_3, S1.Pin_4, R2.Pin_1
  N4: U1.Pin_7, LED1.anode
  N5: U1.Pin_8, BAT2.+, S1.Pin_1, S1.Pin_2, Mod1.Vin
  N6: R1.Pin_1, LED1.cathode

notes:
  PIN 3 ATtiny85 es la salida PWM por defecto. Corresponde a PB4. Sensor KY-005
  Pulsador y resistencia de 10KOhm. PIN5 o PB0
  LED Estado en PB2 o PIN7
  Pila 2025 o 2032, a 3V

custom parts:
  KY-005 Infrared Transmitter Module: Arduino IR Transmitter Module Keyes KY-005, emits infrared light at 38KHz.
