# Fritzing sketch LDR_grabar_datos (saved by Fritzing 0.9.3b)
breadboards: 1

parts:
  R1 = Resistor [tolerance=±5% resistance=4.7k package="0402 [SMD]"]
  Componente1 = Arduino Uno (Rev3) - ICSP
  microSD1 = MicroSD Card Module
  LED1 = smd LED [color="Red (633nm)" package="1206 [SMD]"]
  R2 = Resistor [tolerance=±5% resistance=4.7k package="0402 [SMD]"]  # not connected
  R3 = Resistor [tolerance=±5% resistance=4.7k package="0402 [SMD]"]  # not connected
  R4 = Resistor [tolerance=±5% resistance=680 package="0402 [SMD]"]
  R5 = Photocell (LDR) [package=THT]

nets:
  5V: R1.Pin_0, Componente1.5V, microSD1.VCC
  N1: R1.Pin_1, Componente1.D2, R5.pin_1
  N2: Componente1.ICSP_MISO, Componente1.D12/MISO, microSD1.MISO
  N3: Componente1.D8, microSD1.CS
  N4: Componente1.D11_PWM/MOSI, microSD1.MOSI
  N5: Componente1.D13/SCK, microSD1.SCK
  GND: Componente1.GND, microSD1.GND, R4.Pin_0
  N6: Componente1.D6_PWM, LED1.anode
  N7: LED1.cathode, R4.Pin_1

notes:
  4,7K
  DS18B20
  680
  CS-SCK-MOSI-MISO-VCC-GND
