# Fritzing sketch MotorPAP (saved by Fritzing 0.9.3b)
breadboards: 1

parts:
  Componente1 = Arduino Uno (Rev3)
  IC1 = L293D [package=THT]
  M1 = Stepper Motor - Bipolar

nets:
  N1: Componente1.D8, IC1.In_4
  N2: Componente1.D9_PWM, IC1.In_3
  N3: Componente1.D6_PWM, IC1.In_2
  N4: Componente1.D7, IC1.In_1
  N5: Componente1.GND, IC1.0V
  N6: Componente1.VIN, IC1.Enable_1, IC1.+Vmotor, IC1.Enable_2, IC1.+V
  N7: IC1.Out_1_(_Controlled_by_Enable_1_), M1.C
  N8: IC1.Out_2_(_Controlled_by_Enable_1_), M1.A
  N9: IC1.Out_3_(_Controlled_by_Enable_2_), M1.D
  N10: IC1.Out_4_(_Controlled_by_Enable_2_), M1.B

notes:
  Conecto a Vin, señal de entrada por USB
  La patilla 8 (morado) es la alimentacion del motor
  La patilla 16 (rosa) es la alimentacion del L293D. Debe ser 5V
  Los pines 1 y 9 son señales de ENABLE (5V logica positiva) , cada uno de su lado
