# Fritzing sketch lampara_lectura_UNA (saved by Fritzing 0.9.4)
breadboards: 1

parts:
  U1 = NodeMCU V1.0
  R1 = Resistor [tolerance=±5% resistance=10 package="2512 [SMD]"]
  R2 = Resistor [tolerance=±5% resistance=10 package="2512 [SMD]"]
  U2 = Luxeon LED [package=luxeon]
  Q1 = TRANSISTOR_NPN [package=to-92]
  U3 = Luxeon LED [package=luxeon]
  R3 = Trimmer Potentiometer [maximum_resistance=10kΩ package=THT]

nets:
  N1: U1.3V3, R1.Pin_1, R2.Pin_1, R3.leg1
  N2: U1.GND, Q1.E, R3.leg2
  N3: U1.D5, Q1.B
  N4: U1.A0, R3.wiper
  N5: R1.Pin_0, R2.Pin_0, U2.A, U3.A
  N6: U2.C, Q1.C, U3.C

notes:
  Potenciómetro de 10 KOhm. Control Manual
  LEDs de 1W color blanco
  Q1. PN2222. hfe=135, Vbe = 663mV

custom parts:
  NodeMCU V1.0: ESP8266 based NodeMCU
