# Fritzing sketch lampara_lectura_DOS (saved by Fritzing 0.9.4)
breadboards: 1

parts:
  U1 = NodeMCU V1.0
  R1 = Resistor [tolerance=±5% resistance=10 package="2512 [SMD]"]
  R2 = Resistor [tolerance=±5% resistance=10 package="2512 [SMD]"]
  U2 = Luxeon LED [package=luxeon]
  Q1 = TRANSISTOR_NPN [package=to-92]
  U3 = Luxeon LED [package=luxeon]
  R3 = Trimmer Potentiometer [maximum_resistance=10kΩ package=THT]
  U4 = Luxeon LED [package=luxeon]
  U5 = Luxeon LED [package=luxeon]
  R4 = Resistor [tolerance=±5% resistance=10 package="2512 [SMD]"]
  R5 = Resistor [tolerance=±5% resistance=10 package="2512 [SMD]"]
  Q2 = TRANSISTOR_NPN [package=to-92]
  U6 = SWITCH_SPDT [package=kps-1290]
  R6 = Resistor [tolerance=±5% resistance=10k package="2512 [SMD]"]
  LED1_Piloto_Wifi = LEDs [package=led10mm]
  R7 = Resistor [tolerance=±5% resistance=220 package="2512 [SMD]"]

nets:
  N1: U1.D0, U6.S, R6.Pin_0
  N2: U1.D2, LED1_Piloto_Wifi.A
  N3: U1.3V3, R1.Pin_1, R2.Pin_1, R3.leg1, R4.Pin_1, R5.Pin_1, U6.P
  N4: U1.GND, Q1.E, R3.leg2, Q2.E, R6.Pin_1, R7.Pin_1
  N5: U1.D5, Q1.B
  N6: U1.D8, Q2.B
  N7: U1.A0, R3.wiper
  N8: R1.Pin_0, R2.Pin_0, U2.A, U3.A
  N9: U2.C, Q1.C, U3.C
  N10: U4.A, U5.A, R4.Pin_0, R5.Pin_0
  N11: U4.C, U5.C, Q2.C
  N12: LED1_Piloto_Wifi.C, R7.Pin_0

notes:
  Potenciómetro de 10 KOhm. Control Manual
  LEDs de 1W color blanco. U2, U3, U4 y U5
  Q1. Q2. PN2222. hfe=135, Vbe = 663mV
  U6. Switch que conecta en modo manual la lámpara izquierda o derecha

custom parts:
  NodeMCU V1.0: ESP8266 based NodeMCU
